// Logisim project AiAlu.circ as structural Verilog
module AiAlu_interface (
  input  [7:0] A,
  input  [7:0] B,
  input  [2:0] Operation_select,
  output [7:0] Bin_result
);

  wire aialu_subcircuit_1_clock, aialu_subcircuit_1_cls_2, aialu_subcircuit_1_standby, tunnel;
  wire [6:0] aialu_subcircuit_1_sysoutput;

  Button button_1 (.out(tunnel));
  TTY #(.rows(2)) tty_1 (
    .data(aialu_subcircuit_1_sysoutput), .clk(aialu_subcircuit_1_clock), .clr(aialu_subcircuit_1_cls_2));  // open: we
  LED POWER (.in(aialu_subcircuit_1_standby));
  // Probe on Bin_result
  aiAlu_Subcircuit aialu_subcircuit_1 (
    .in_1(Operation_select), .A(A), .B(B), .Output(Bin_result), .StandBy(aialu_subcircuit_1_standby),
    .Cls(tunnel), .SysOutput(aialu_subcircuit_1_sysoutput), .Clock(aialu_subcircuit_1_clock),
    .CLS_2(aialu_subcircuit_1_cls_2));

  // Other names for the same wires on the sheet: O[2:0] = Operation_select
endmodule

module aiAlu_Subcircuit (
  input  [2:0] in_1,
  input  [7:0] A,
  input  [7:0] B,
  input  Cls,
  output [7:0] Output,
  output StandBy,
  output CLS_2,
  output Clock,
  output [6:0] SysOutput
);

  wire and_1_out, arithunit_1_out_18, clock_1_out, lbc_message_displayer_1_out_4;
  wire [1:0] decoder_1_i0;
  wire [4:0] decoder_1_i2;
  wire [7:0] arithunit_1_out_19, logicunit_1_out_4;

  Decoder decoder_1 (
    .O0(in_1[2]), .O1(in_1[1]), .O2(in_1[0]), .I7_2600K(StandBy), .I6(decoder_1_i2[4]), .I5(decoder_1_i2[3]),
    .I4(decoder_1_i2[2]), .I3(decoder_1_i2[1]), .I2(decoder_1_i2[0]), .I1(decoder_1_i0[1]),
    .I0(decoder_1_i0[0]));
  Clock clock_1 (.out(clock_1_out));
  LBC_message_displayer lbc_message_displayer_1 (
    .out_3(SysOutput), .Clear(Cls), .Over(arithunit_1_out_18), .out_4(lbc_message_displayer_1_out_4));
  and and_1 (and_1_out, arithunit_1_out_18, clock_1_out);
  LogicUnit logicunit_1 (.in_1(decoder_1_i2), .A(A), .B(B), .out_4(logicunit_1_out_4));
  and and_2 (Clock, and_1_out, lbc_message_displayer_1_out_4);
  ArithUnit arithunit_1 (
    .a0(A[0]), .a1(A[1]), .a2(A[2]), .a3(A[3]), .a4(A[4]), .a5(A[5]), .a6(A[6]), .a7(A[7]), .b0(B[0]),
    .b1(B[1]), .b2(B[2]), .b3(B[3]), .b4(B[4]), .b5(B[5]), .b6(B[6]), .b7(B[7]), .out_19(arithunit_1_out_19),
    .in_17(decoder_1_i0), .out_18(arithunit_1_out_18));
  Result_Confirmer result_confirmer_1 (
    .a0(arithunit_1_out_19[0]), .a1(arithunit_1_out_19[1]), .a2(arithunit_1_out_19[2]),
    .a3(arithunit_1_out_19[3]), .a4(arithunit_1_out_19[4]), .a5(arithunit_1_out_19[5]),
    .a6(arithunit_1_out_19[6]), .a7(arithunit_1_out_19[7]), .b0(logicunit_1_out_4[0]),
    .b1(logicunit_1_out_4[1]), .b2(logicunit_1_out_4[2]), .b3(logicunit_1_out_4[3]),
    .b4(logicunit_1_out_4[4]), .b5(logicunit_1_out_4[5]), .b6(logicunit_1_out_4[6]),
    .b7(logicunit_1_out_4[7]), .out_17(Output));

  assign CLS_2 = Cls;
endmodule

module ArithUnit (
  input  a0,
  input  a1,
  input  a2,
  input  a3,
  input  a4,
  input  a5,
  input  a6,
  input  a7,
  input  b0,
  input  b1,
  input  b2,
  input  b3,
  input  b4,
  input  b5,
  input  b6,
  input  b7,
  input  [1:0] in_17,
  output out_18,
  output [7:0] out_19
);

  wire button_1_out, processor_enabler_1_out0, processor_enabler_1_out1, processor_enabler_1_out2,
       processor_enabler_1_out3, processor_enabler_1_out4, processor_enabler_1_out5,
       processor_enabler_1_out6, processor_enabler_1_out7, processor_enabler_2_out0,
       processor_enabler_2_out1, processor_enabler_2_out2, processor_enabler_2_out3,
       processor_enabler_2_out4, processor_enabler_2_out5, processor_enabler_2_out6,
       processor_enabler_2_out7, processor_enabler_aux_1_out0, processor_enabler_aux_1_out1,
       processor_enabler_aux_1_out2, processor_enabler_aux_1_out3, processor_enabler_aux_1_out4,
       processor_enabler_aux_1_out5, processor_enabler_aux_1_out6, processor_enabler_aux_1_out7,
       processor_enabler_aux_2_out0, processor_enabler_aux_2_out1, processor_enabler_aux_2_out2,
       processor_enabler_aux_2_out3, processor_enabler_aux_2_out4, processor_enabler_aux_2_out5,
       processor_enabler_aux_2_out6, processor_enabler_aux_2_out7;
  wire [7:0] cpl2_1_y0, intel_adder_inside_1_y0;

  Button button_1 (.out(button_1_out));
  Processor_Enabler processor_enabler_1 (
    .Processor_Check(in_17[0]), .IN0(a0), .IN1(a1), .IN2(a2), .IN3(a3), .IN4(a4), .IN5(a5), .IN6(a6),
    .IN7(a7), .OUT0(processor_enabler_1_out0), .OUT1(processor_enabler_1_out1),
    .OUT2(processor_enabler_1_out2), .OUT3(processor_enabler_1_out3), .OUT4(processor_enabler_1_out4),
    .OUT5(processor_enabler_1_out5), .OUT6(processor_enabler_1_out6), .OUT7(processor_enabler_1_out7));
  Intel_Adder_Inside intel_adder_inside_1 (
    .c(button_1_out), .a0(processor_enabler_1_out0), .a1(processor_enabler_1_out1),
    .a2(processor_enabler_1_out2), .a3(processor_enabler_1_out3), .a4(processor_enabler_1_out4),
    .a5(processor_enabler_1_out5), .b0(processor_enabler_aux_1_out0), .a6(processor_enabler_1_out6),
    .b1(processor_enabler_aux_1_out1), .a7(processor_enabler_1_out7), .b2(processor_enabler_aux_1_out2),
    .b4(processor_enabler_aux_1_out4), .b5(processor_enabler_aux_1_out5), .b3(processor_enabler_aux_1_out3),
    .b6(processor_enabler_aux_1_out6), .b7(processor_enabler_aux_1_out7), .Resto(out_18),
    .y0(intel_adder_inside_1_y0[0]), .y1(intel_adder_inside_1_y0[1]), .y2(intel_adder_inside_1_y0[2]),
    .y3(intel_adder_inside_1_y0[3]), .y4(intel_adder_inside_1_y0[4]), .y5(intel_adder_inside_1_y0[5]),
    .y6(intel_adder_inside_1_y0[6]), .y7(intel_adder_inside_1_y0[7]));
  Processor_Enabler_AUX processor_enabler_aux_1 (
    .Processor_Check(in_17[0]), .IN0(b0), .IN1(b1), .IN2(b2), .IN3(b3), .IN4(b4), .IN5(b5), .IN6(b6),
    .IN7(b7), .OUT0(processor_enabler_aux_1_out0), .OUT1(processor_enabler_aux_1_out1),
    .OUT2(processor_enabler_aux_1_out2), .OUT3(processor_enabler_aux_1_out3),
    .OUT4(processor_enabler_aux_1_out4), .OUT5(processor_enabler_aux_1_out5),
    .OUT6(processor_enabler_aux_1_out6), .OUT7(processor_enabler_aux_1_out7));
  Processor_Enabler processor_enabler_2 (
    .Processor_Check(in_17[1]), .IN0(a0), .IN1(a1), .IN2(a2), .IN3(a3), .IN4(a4), .IN5(a5), .IN6(a6),
    .IN7(a7), .OUT0(processor_enabler_2_out0), .OUT1(processor_enabler_2_out1),
    .OUT2(processor_enabler_2_out2), .OUT3(processor_enabler_2_out3), .OUT4(processor_enabler_2_out4),
    .OUT5(processor_enabler_2_out5), .OUT6(processor_enabler_2_out6), .OUT7(processor_enabler_2_out7));
  Cpl2 cpl2_1 (
    .a0(processor_enabler_2_out0), .a1(processor_enabler_2_out1), .a2(processor_enabler_2_out2),
    .a3(processor_enabler_2_out3), .a4(processor_enabler_2_out4), .a5(processor_enabler_2_out5),
    .a6(processor_enabler_2_out6), .a7(processor_enabler_2_out7), .b0(processor_enabler_aux_2_out0),
    .b1(processor_enabler_aux_2_out1), .b2(processor_enabler_aux_2_out2), .b3(processor_enabler_aux_2_out3),
    .b4(processor_enabler_aux_2_out4), .b5(processor_enabler_aux_2_out5), .b6(processor_enabler_aux_2_out6),
    .b7(processor_enabler_aux_2_out7), .y0(cpl2_1_y0[0]), .y1(cpl2_1_y0[1]), .y2(cpl2_1_y0[2]),
    .y3(cpl2_1_y0[3]), .y4(cpl2_1_y0[4]), .y5(cpl2_1_y0[5]), .y6(cpl2_1_y0[6]), .y7(cpl2_1_y0[7]),
    .c(button_1_out));  // open: OVER
  Processor_Enabler_AUX processor_enabler_aux_2 (
    .Processor_Check(in_17[1]), .IN0(b0), .IN1(b1), .IN2(b2), .IN3(b3), .IN4(b4), .IN5(b5), .IN6(b6),
    .IN7(b7), .OUT0(processor_enabler_aux_2_out0), .OUT1(processor_enabler_aux_2_out1),
    .OUT2(processor_enabler_aux_2_out2), .OUT3(processor_enabler_aux_2_out3),
    .OUT4(processor_enabler_aux_2_out4), .OUT5(processor_enabler_aux_2_out5),
    .OUT6(processor_enabler_aux_2_out6), .OUT7(processor_enabler_aux_2_out7));
  Result_Confirmer result_confirmer_1 (
    .a0(intel_adder_inside_1_y0[0]), .a1(intel_adder_inside_1_y0[1]), .a2(intel_adder_inside_1_y0[2]),
    .a3(intel_adder_inside_1_y0[3]), .a4(intel_adder_inside_1_y0[4]), .a5(intel_adder_inside_1_y0[5]),
    .a6(intel_adder_inside_1_y0[6]), .a7(intel_adder_inside_1_y0[7]), .b0(cpl2_1_y0[0]), .b1(cpl2_1_y0[1]),
    .b2(cpl2_1_y0[2]), .b3(cpl2_1_y0[3]), .b4(cpl2_1_y0[4]), .b5(cpl2_1_y0[5]), .b6(cpl2_1_y0[6]),
    .b7(cpl2_1_y0[7]), .out_17(out_19));
endmodule

module Cpl2 (
  input  a0,
  input  a1,
  input  a2,
  input  a3,
  input  a4,
  input  a5,
  input  a6,
  input  a7,
  input  b0,
  input  c,
  input  b1,
  input  b2,
  input  b3,
  input  b4,
  input  b5,
  input  b6,
  input  b7,
  output OVER,
  output y0,
  output y1,
  output y2,
  output y3,
  output y4,
  output y5,
  output y6,
  output y7
);

  wire intel_adder_inside_1_y0, intel_adder_inside_1_y1, intel_adder_inside_1_y2, intel_adder_inside_1_y3,
       intel_adder_inside_1_y4, intel_adder_inside_1_y5, intel_adder_inside_1_y6, intel_adder_inside_1_y7,
       not_1_out, not_2_out, not_3_out, not_4_out, not_5_out, not_6_out, not_7_out, not_8_out;

  not not_1 (not_1_out, b0);
  not not_2 (not_2_out, b1);
  not not_3 (not_3_out, b2);
  not not_4 (not_4_out, b3);
  not not_5 (not_5_out, b4);
  not not_6 (not_6_out, b5);
  not not_7 (not_7_out, b6);
  not not_8 (not_8_out, b7);
  Intel_Adder_Inside intel_adder_inside_1 (
    .c(1'b1), .a0(1'b0), .a1(1'b0), .a2(1'b0), .a3(1'b0), .a4(1'b0), .a5(1'b0), .b0(not_1_out), .a6(1'b0),
    .b1(not_2_out), .a7(1'b0), .b2(not_3_out), .b4(not_5_out), .b5(not_6_out), .b3(not_4_out),
    .b6(not_7_out), .b7(not_8_out), .y0(intel_adder_inside_1_y0), .y1(intel_adder_inside_1_y1),
    .y2(intel_adder_inside_1_y2), .y3(intel_adder_inside_1_y3), .y4(intel_adder_inside_1_y4),
    .y5(intel_adder_inside_1_y5), .y6(intel_adder_inside_1_y6), .y7(intel_adder_inside_1_y7));  // open: Resto
  Intel_Adder_Inside intel_adder_inside_2 (
    .c(c), .a0(a0), .a1(a1), .a2(a2), .a3(a3), .a4(a4), .a5(a5), .b0(intel_adder_inside_1_y0), .a6(a6),
    .b1(intel_adder_inside_1_y1), .a7(a7), .b2(intel_adder_inside_1_y2), .b4(intel_adder_inside_1_y4),
    .b5(intel_adder_inside_1_y5), .b3(intel_adder_inside_1_y3), .b6(intel_adder_inside_1_y6),
    .b7(intel_adder_inside_1_y7), .Resto(OVER), .y0(y0), .y1(y1), .y2(y2), .y3(y3), .y4(y4), .y5(y5),
    .y6(y6), .y7(y7));
endmodule

module and8bit (
  input  [7:0] andA,
  input  [7:0] andB,
  output [7:0] andY
);

  assign andY = andA & andB;  // AND_Gate and_1, 8 bits wide
endmodule

module or8bit (
  input  [7:0] orA,
  input  [7:0] orB,
  output [7:0] orY
);

  assign orY = orA | orB;  // OR_Gate or_1, 8 bits wide
endmodule

module not8bit (
  input  [7:0] notA,
  input  enableA,
  input  [7:0] notB,
  input  enableA_2,
  output [7:0] out_5
);

  wire [7:0] and_1_out, and_2_out, not_1_out, not_2_out;

  assign not_1_out = ~notA;  // NOT_Gate not_1, 8 bits wide
  assign and_1_out = not_1_out & {8{enableA}};  // AND_Gate and_1, 8 bits wide
  assign not_2_out = ~notB;  // NOT_Gate not_2, 8 bits wide
  assign and_2_out = not_2_out & {8{enableA_2}};  // AND_Gate and_2, 8 bits wide
  assign out_5 = and_1_out | and_2_out;  // OR_Gate or_1, 8 bits wide
endmodule

// Integrated Processor Enabler
module Processor_Enabler (
  input  IN0,
  input  IN1,
  input  IN2,
  input  IN3,
  input  IN4,
  input  IN5,
  input  IN6,
  input  IN7,
  input  Processor_Check,
  output OUT0,
  output OUT1,
  output OUT2,
  output OUT3,
  output OUT4,
  output OUT5,
  output OUT6,
  output OUT7
);

  and and_1 (OUT2, Processor_Check, IN2);
  and and_2 (OUT0, Processor_Check, IN0);
  and and_3 (OUT1, Processor_Check, IN1);
  and and_4 (OUT4, Processor_Check, IN4);
  and and_5 (OUT3, Processor_Check, IN3);
  and and_6 (OUT5, Processor_Check, IN5);
  and and_7 (OUT7, Processor_Check, IN7);
  and and_8 (OUT6, Processor_Check, IN6);
endmodule

// Integrated Processor Enabler
module Processor_Enabler_AUX (
  input  IN0,
  input  IN1,
  input  IN2,
  input  IN3,
  input  IN4,
  input  IN5,
  input  IN6,
  input  IN7,
  input  Processor_Check,
  output OUT0,
  output OUT1,
  output OUT2,
  output OUT3,
  output OUT4,
  output OUT5,
  output OUT6,
  output OUT7
);

  and and_1 (OUT0, Processor_Check, IN0);
  and and_2 (OUT2, Processor_Check, IN2);
  and and_3 (OUT1, Processor_Check, IN1);
  and and_4 (OUT4, Processor_Check, IN4);
  and and_5 (OUT5, Processor_Check, IN5);
  and and_6 (OUT3, Processor_Check, IN3);
  and and_7 (OUT7, Processor_Check, IN7);
  and and_8 (OUT6, Processor_Check, IN6);
endmodule

module Operation_Selector (
  input  I0,
  input  I1,
  output S0,
  output S1,
  output S2,
  output S3
);

  wire not_1_out, not_2_out;

  not not_1 (not_1_out, I0);
  not not_2 (not_2_out, I1);
  and and_1 (S0, not_1_out, not_2_out);
  and and_2 (S1, not_1_out, I1);
  and and_3 (S2, not_2_out, I0);
  and and_4 (S3, I1, I0);
endmodule

// Integrated Result Confirmer
module Result_Confirmer (
  input  a0,
  input  a1,
  input  a2,
  input  a3,
  input  a4,
  input  a5,
  input  a6,
  input  a7,
  input  b0,
  input  b1,
  input  b2,
  input  b3,
  input  b4,
  input  b5,
  input  b6,
  input  b7,
  output [7:0] out_17
);

  or or_1 (out_17[0], a0, b0);
  or or_2 (out_17[1], a1, b1);
  or or_3 (out_17[2], a2, b2);
  or or_4 (out_17[3], a3, b3);
  or or_5 (out_17[4], a4, b4);
  or or_6 (out_17[5], a5, b5);
  or or_7 (out_17[6], a6, b6);
  or or_8 (out_17[7], a7, b7);
endmodule

module Intel_Adder_Inside (
  input  c,
  input  a0,
  input  a1,
  input  a2,
  input  a3,
  input  a4,
  input  a5,
  input  b0,
  input  a6,
  input  b1,
  input  a7,
  input  b2,
  input  b4,
  input  b5,
  input  b3,
  input  b6,
  input  b7,
  output Resto,
  output y0,
  output y1,
  output y2,
  output y3,
  output y4,
  output y5,
  output y6,
  output y7
);

  wire n4_bit_adder_processor_1_c_2;

  _4_bit_adder_processor u_4_bit_adder_processor_1 (
    .c(c), .a0(a0), .a1(a1), .a2(a2), .a3(a3), .b0(b0), .b1(b1), .b2(b2), .b3(b3), .s0(y0), .s1(y1), .s2(y2),
    .s3(y3), .C_2(n4_bit_adder_processor_1_c_2));
  _4_bit_adder_processor u_4_bit_adder_processor_2 (
    .c(n4_bit_adder_processor_1_c_2), .a0(a4), .a1(a5), .a2(a6), .a3(a7), .b0(b4), .b1(b5), .b2(b6), .b3(b7),
    .s0(y4), .s1(y5), .s2(y6), .s3(y7), .C_2(Resto));
endmodule

module Full_Adder_Subsystem (
  input  c0,
  input  a,
  input  b,
  output S,
  output C
);

  wire and_1_out, and_2_out, and_3_out, xor_1_out;

  and and_1 (and_1_out, b, a);
  xor xor_1 (xor_1_out, a, b);
  xor xor_2 (S, xor_1_out, c0);
  and and_2 (and_2_out, c0, a);
  and and_3 (and_3_out, c0, b);
  or or_1 (C, and_1_out, and_2_out, and_3_out);
endmodule

module _4_bit_adder_processor (
  input  c,
  input  a0,
  input  a1,
  input  a2,
  input  a3,
  input  b0,
  input  b1,
  input  b2,
  input  b3,
  output s0,
  output s1,
  output s2,
  output s3,
  output C_2
);

  wire full_adder_subsystem_1_c, full_adder_subsystem_2_c, full_adder_subsystem_3_c;

  Full_Adder_Subsystem full_adder_subsystem_1 (.c0(c), .a(a0), .b(b0), .S(s0), .C(full_adder_subsystem_1_c));
  Full_Adder_Subsystem full_adder_subsystem_2 (
    .c0(full_adder_subsystem_1_c), .a(a1), .b(b1), .S(s1), .C(full_adder_subsystem_2_c));
  Full_Adder_Subsystem full_adder_subsystem_3 (
    .c0(full_adder_subsystem_2_c), .a(a2), .b(b2), .S(s2), .C(full_adder_subsystem_3_c));
  Full_Adder_Subsystem full_adder_subsystem_4 (.c0(full_adder_subsystem_3_c), .a(a3), .b(b3), .S(s3), .C(C_2));
endmodule

module exor8bit (
  input  [7:0] exorA,
  input  [7:0] exorB,
  output [7:0] exorY
);

  assign exorY = exorA ^ exorB;  // XOR_Gate xor_1, 8 bits wide
endmodule

module LogicUnit (
  input  [4:0] in_1,
  input  [7:0] A,
  input  [7:0] B,
  output [7:0] out_4
);

  wire or_1_out;
  wire [7:0] and8bit_1_andy, exor8bit_1_exory, logicunit_abilitator_1_uscita, logicunit_abilitator_2_uscita,
       logicunit_abilitator_3_uscita, logicunit_abilitator_4_uscita, not8bit_1_out_5, or8bit_1_ory;

  or or_1 (or_1_out, in_1[2], in_1[3]);
  and8bit and8bit_1 (.andA(A), .andB(B), .andY(and8bit_1_andy));
  or8bit or8bit_1 (.orA(A), .orB(B), .orY(or8bit_1_ory));
  not8bit not8bit_1 (.notA(A), .enableA(in_1[2]), .notB(B), .out_5(not8bit_1_out_5), .enableA_2(in_1[3]));
  exor8bit exor8bit_1 (.exorA(A), .exorB(B), .exorY(exor8bit_1_exory));
  LogicUnit_Abilitator logicunit_abilitator_1 (
    .Ingresso(and8bit_1_andy), .Abi(in_1[0]), .Uscita(logicunit_abilitator_1_uscita));
  LogicUnit_Abilitator logicunit_abilitator_2 (
    .Ingresso(or8bit_1_ory), .Abi(in_1[1]), .Uscita(logicunit_abilitator_2_uscita));
  LogicUnit_Abilitator logicunit_abilitator_3 (
    .Ingresso(not8bit_1_out_5), .Abi(or_1_out), .Uscita(logicunit_abilitator_3_uscita));
  LogicUnit_Abilitator logicunit_abilitator_4 (
    .Ingresso(exor8bit_1_exory), .Abi(in_1[4]), .Uscita(logicunit_abilitator_4_uscita));
  assign out_4 = logicunit_abilitator_1_uscita | logicunit_abilitator_2_uscita | logicunit_abilitator_3_uscita | logicunit_abilitator_4_uscita;  // OR_Gate or_2, 8 bits wide
endmodule

module Decoder (
  input  O0,
  input  O1,
  input  O2,
  output I7_2600K,
  output I6,
  output I5,
  output I4,
  output I3,
  output I2,
  output I1,
  output I0
);

  wire not_1_out, not_2_out, not_3_out;

  not not_1 (not_1_out, O0);
  not not_2 (not_2_out, O1);
  not not_3 (not_3_out, O2);
  and and_1 (I7_2600K, O0, O1, O2);
  and and_2 (I6, O0, O1, not_3_out);
  and and_3 (I5, O0, not_2_out, O2);
  and and_4 (I4, O0, not_2_out, not_3_out);
  and and_5 (I2, not_1_out, O1, not_3_out);
  and and_6 (I3, not_1_out, O1, O2);
  and and_7 (I1, not_1_out, not_2_out, O2);
  and and_8 (I0, not_1_out, not_2_out, not_3_out);
endmodule

// Unit Abilitator
module LogicUnit_Abilitator (
  input  [7:0] Ingresso,
  input  Abi,
  output [7:0] Uscita
);

  and and_1 (Uscita[0], Abi, Ingresso[0]);
  and and_2 (Uscita[1], Abi, Ingresso[1]);
  and and_3 (Uscita[2], Abi, Ingresso[2]);
  and and_4 (Uscita[3], Abi, Ingresso[3]);
  and and_5 (Uscita[5], Abi, Ingresso[5]);
  and and_6 (Uscita[4], Abi, Ingresso[4]);
  and and_7 (Uscita[7], Abi, Ingresso[7]);
  and and_8 (Uscita[6], Abi, Ingresso[6]);
endmodule

module LBC_message_displayer (
  input  Clear,
  input  Over,
  output [6:0] out_3,
  output out_4
);

  wire and_1_out, and_2_out, and_3_out, and_4_out, clock_1_out, clock_2_out, j_k_ff_1_qn, j_k_ff_2_qn,
       j_k_ff_3_qn, not_1_out;
  wire [2:0] not_2_out;

  and and_1 (and_1_out, and_2_out, not_1_out);
  not not_1 (not_1_out, and_4_out);
  and and_2 (and_2_out, clock_1_out, Over);
  Clock clock_1 (.out(clock_1_out));
  Clock clock_2 (.out(clock_2_out));
  J_K_Flip_Flop j_k_ff_1 (.J(1'b1), .clk(and_1_out), .K(1'b1), .Qn(j_k_ff_1_qn), .reset(Clear));  // open: Q, preset, en
  not not_2 (not_2_out[0], j_k_ff_1_qn);
  not not_3 (not_2_out[1], j_k_ff_2_qn);
  not not_4 (not_2_out[2], j_k_ff_3_qn);
  J_K_Flip_Flop j_k_ff_2 (
    .J(1'b1), .clk(j_k_ff_1_qn), .K(1'b1), .Qn(j_k_ff_2_qn), .reset(Clear));  // open: Q, preset, en
  ROM #(.addrWidth(3), .dataWidth(7)) rom_1 (.addr(not_2_out), .data(out_3), .sel(1'b1));
  and and_3 (and_3_out, and_1_out, clock_2_out);
  J_K_Flip_Flop j_k_ff_3 (
    .J(1'b1), .clk(j_k_ff_2_qn), .K(1'b1), .Qn(j_k_ff_3_qn), .reset(Clear));  // open: Q, preset, en
  and and_4 (and_4_out, not_2_out[2], not_2_out[1], not_2_out[0]);
  not not_5 (out_4, and_4_out);
  TTY tty_1 (.data(out_3), .clk(and_3_out), .clr(Clear));  // open: we

  // Notes on the sheet:
  //   contents of rom_1 (hex, n*v repeats v):
  //   4f 76 72 6c 6f 61 64 20
endmodule

module Overload_Adder (
  input  MSB1,
  input  MSB2,
  input  MSBr,
  output Overload
);

  wire and_1_out, and_2_out, and_3_out, not_1_out, not_2_out, not_3_out, not_4_out;

  not not_1 (not_1_out, MSB1);
  not not_2 (not_2_out, MSB1);
  not not_3 (not_3_out, MSB2);
  not not_4 (not_4_out, MSBr);
  and and_1 (and_1_out, not_1_out, MSBr);
  and and_2 (and_2_out, not_2_out, MSB2);
  and and_3 (and_3_out, MSB1, not_3_out, not_4_out);
  or or_1 (Overload, and_1_out, and_2_out, and_3_out);
endmodule
